// Logisim project ALU_4bit.circ as structural Verilog: 2 circuits, main circuit main
module main (
  input  S1,
  input  S0,
  input  A0,
  input  in_4,
  input  in_5,
  input  in_6,
  input  in_7,
  input  B0,
  input  in_9,
  input  in_10,
  input  B,
  output O3,
  output O2,
  output O1,
  output Output0,
  output Carry_out
);

  _4Bit_ALU _4_bit_ALU (
    .OS0(S0), .OS1(S1), .A0(A0), .A1(in_4), .A2(in_5), .A3(in_6), .B0(B0), .B1(in_9), .B2(in_10), .in_10(B),
    .in_11(in_7), .out_16(Carry_out), .out_12(O3), .out_15(O2), .out_13(O1), .out_14(Output0));

  // Notes on the sheet:
  //   0 0 = A or B
  //    0 1 = A + B
  //   1 0 = A and B
  //   1 1= A'
  //   ALU
  //   Turn into subtraction 2s complement
endmodule

module _4Bit_ALU (
  input  OS0,
  input  OS1,
  input  A0,
  input  A1,
  input  A2,
  input  A3,
  input  B0,
  input  B1,
  input  B2,
  input  in_10,
  input  in_11,
  output out_12,
  output out_13,
  output out_14,
  output out_15,
  output out_16
);

  wire A0__B0_out, A0_B0_2_out, A0_B0_out, A0_prime_2_out, A0_prime_out, A1___B1_2_out, A1___B1_out,
       A1_B1_2_out, A1_B1_3_out, A1_B1_4_out, A1_B1_out, A1_OR_B0_2_out, A1_OR_B0_out, A1_prime_2_out,
       A1_prime_3_out, A1_prime_out, A2__B2_out, A2_B2_2_out, A2_B2_3_out, A2_B2_4_out, A2_B2_5_out,
       A2_B2_out, A2_OR_B2_out, A2_prime_2_out, A2_prime_3_out, A2_prime_out, A___B_out, and_2_out,
       and_3_out, and_4_out, and_5_out, and_6_out, and_7_out, and_8_out, and_9_out, and_10_out, C2_out,
       C3_2_out, C3_out, not_1_out, not_2_out, or_5_out, S1_out, S2_2_out, S2_out, Sum_2_out, Sum_3_out,
       Sum_out, xor_1_out, xor_2_out, xor_3_out, xor_4_out, xor_5_out, xor_6_out;

  not not_1 (not_1_out, OS0);
  not not_2 (not_2_out, OS1);
  and A0__B0 (A0__B0_out, A0, B0);
  not A0_prime (A0_prime_out, A0);
  and and_1 (out_16, not_2_out, OS0, C3_2_out);
  or A0_B0 (A0_B0_out, A0, B0);
  and A1_B1 (A1_B1_out, A1, B1);
  not A1_prime (A1_prime_out, A1);
  and A1_prime_2 (A1_prime_2_out, OS0, OS1, A2_prime_3_out);
  or A1_B1_2 (A1_B1_2_out, A1, B1);
  or or_1 (out_12, A1_prime_2_out, A1_B1_3_out, A1_OR_B0_out, A1___B1_out);
  and A1_B1_3 (A1_B1_3_out, OS1, not_1_out, A2_B2_4_out);
  and A1_OR_B0 (A1_OR_B0_out, not_2_out, A2_B2_5_out, not_1_out);
  and A2_B2 (A2_B2_out, A2, B2);
  not A2_prime (A2_prime_out, A2);
  and A1___B1 (A1___B1_out, not_2_out, OS0, S2_2_out);
  or A2_B2_2 (A2_B2_2_out, A2, B2);
  and A2_prime_2 (A2_prime_2_out, OS0, A2_prime_out, OS1);
  and A2_B2_3 (A2_B2_3_out, not_1_out, OS1, A2_B2_out);
  and A2_B2_4 (A2_B2_4_out, A3, in_10);
  not A2_prime_3 (A2_prime_3_out, A3);
  or or_2 (out_15, A2_prime_2_out, A2_B2_3_out, A2_OR_B2_out, A2__B2_out);
  and A2_OR_B2 (A2_OR_B2_out, A2_B2_2_out, not_2_out, not_1_out);
  or A2_B2_5 (A2_B2_5_out, A3, in_10);
  and A2__B2 (A2__B2_out, OS0, not_2_out, S2_out);
  and A1_prime_3 (A1_prime_3_out, OS0, OS1, A1_prime_out);
  or or_3 (out_13, A1_prime_3_out, A1_B1_4_out, A1_OR_B0_2_out, A1___B1_2_out);
  and A1_B1_4 (A1_B1_4_out, not_1_out, OS1, A1_B1_out);
  and A1_OR_B0_2 (A1_OR_B0_2_out, A1_B1_2_out, not_1_out, not_2_out);
  xor xor_1 (xor_1_out, B0, in_11);
  xor xor_2 (xor_2_out, B1, in_11);
  xor xor_3 (xor_3_out, B2, in_11);
  xor xor_4 (xor_4_out, in_10, in_11);
  and A1___B1_2 (A1___B1_2_out, not_2_out, OS0, S1_out);
  and A0_prime_2 (A0_prime_2_out, OS0, OS1, A0_prime_out);
  or or_4 (out_14, A0_prime_2_out, A0_B0_2_out, and_2_out, A___B_out);
  and A0_B0_2 (A0_B0_2_out, OS1, not_1_out, A0__B0_out);
  and and_2 (and_2_out, not_1_out, not_2_out, A0_B0_out);
  and A___B (A___B_out, OS0, not_2_out, xor_6_out);
  xor xor_5 (xor_5_out, A0, xor_1_out);
  and and_3 (and_3_out, A0, xor_1_out);
  and and_4 (and_4_out, xor_5_out, in_11);
  xor Sum (Sum_out, xor_2_out, A1);
  and and_5 (and_5_out, xor_2_out, A1);
  xor Sum_2 (Sum_2_out, A2, xor_3_out);
  and and_6 (and_6_out, A2, xor_3_out);
  xor Sum_3 (Sum_3_out, A3, xor_4_out);
  and and_7 (and_7_out, A3, xor_4_out);
  and and_8 (and_8_out, or_5_out, Sum_out);
  and and_9 (and_9_out, C2_out, Sum_2_out);
  and and_10 (and_10_out, C3_out, Sum_3_out);
  xor xor_6 (xor_6_out, xor_5_out, in_11);
  or or_5 (or_5_out, and_4_out, and_3_out);
  xor S1 (S1_out, or_5_out, Sum_out);
  or C2 (C2_out, and_8_out, and_5_out);
  xor S2 (S2_out, C2_out, Sum_2_out);
  or C3 (C3_out, and_9_out, and_6_out);
  xor S2_2 (S2_2_out, C3_out, Sum_3_out);
  or C3_2 (C3_2_out, and_10_out, and_7_out);

  // Notes on the sheet:
  //   Output Selector
  //   ALU Circuit Diagram 
  //   By Ricky Flores
  //   C0 (Add/Sub Input)
  //   Carry Out
  //   4X1 Multiplexr for position 1
  //   Output 3
  //   Creates complement of B if C0 =1
  //   Adds 1 to make 2s complement
  //   4X1 Multiplexr for position 1
  //   Output 2
  //   4X1 Multiplexr for position 1
  //   Carry Out 
  //   last Carry out
  //   C0
  //   Output 1
  //   A input
  //   Output 0
  //   Full Adder and Subtractor
  //   Collum 0 
  //   A OR B
  //   0 0
  //   4 x 1 Multiplexer for position 0
  //   1 0
  //   OS0 OS1
  //   1+1 = 0
  //   Creates carry if 1 + 1
  //   2nd Collumn/2nd Half adder >
  //   1 + 1 = 0
  //   Carry if A and B = 1
  //   1 + 1 = 0
  //   Carry if A and B = 1
  //   1 + 1 = 0
  //   Carry if A and B = 1
  //   if 1 + 0 + 1 = 0 + 1 carry
  //   Carry if sum =1 carry =1
  //   Carry if sum =1 carry =1
  //   Carry if sum =1 carry =1
  //   sum + carry
  //   sum + carry
  //   sum + carry
  //   S0 [Sum]
  //   C1 [Carry]
  //   Outputs
  //   S0
  //   S1
endmodule
