// Logisim project Flores_8bitALU_RegisterCopyandWrite.circ as structural Verilog: 2 circuits, main circuit 8Bit ALU + Registers
module _8_bit_ALU (
  input  in_1,
  input  in_2,
  input  A0,
  input  A1,
  input  A2,
  input  A3,
  input  A0_2,
  input  A1_2,
  input  A2_2,
  input  A3_2,
  input  B0,
  input  B1,
  input  B2,
  input  in_14,
  input  B0_2,
  input  B1_2,
  input  B2_2,
  input  in_18,
  input  in_19,
  output out_20,
  output out_21,
  output out_22,
  output out_23,
  output out_24,
  output out_25,
  output out_26,
  output out_27,
  output out_28
);

  wire A0__B0_2_out, A0__B0_out, A0_B0_2_out, A0_B0_3_out, A0_B0_4_out, A0_B0_out, A0_prime_2_out,
       A0_prime_3_out, A0_prime_4_out, A0_prime_out, A1___B1_2_out, A1___B1_3_out, A1___B1_4_out,
       A1___B1_out, A1_B1_2_out, A1_B1_3_out, A1_B1_4_out, A1_B1_5_out, A1_B1_6_out, A1_B1_7_out,
       A1_B1_8_out, A1_B1_out, A1_OR_B0_2_out, A1_OR_B0_3_out, A1_OR_B0_4_out, A1_OR_B0_out, A1_prime_2_out,
       A1_prime_3_out, A1_prime_4_out, A1_prime_5_out, A1_prime_6_out, A1_prime_out, A2__B2_2_out,
       A2__B2_out, A2_B2_2_out, A2_B2_3_out, A2_B2_4_out, A2_B2_5_out, A2_B2_6_out, A2_B2_7_out, A2_B2_8_out,
       A2_B2_9_out, A2_B2_10_out, A2_B2_out, A2_OR_B2_2_out, A2_OR_B2_out, A2_prime_2_out, A2_prime_3_out,
       A2_prime_4_out, A2_prime_5_out, A2_prime_6_out, A2_prime_out, A___B_2_out, A___B_out, and_1_out,
       and_2_out, and_4_out, and_5_out, and_6_out, and_7_out, and_8_out, and_9_out, and_10_out, and_11_out,
       and_12_out, and_13_out, and_14_out, and_15_out, and_16_out, and_17_out, and_18_out, and_19_out,
       C2_2_out, C2_out, C3_2_out, C3_3_out, C3_4_out, C3_5_out, C3_out, not_1_out, not_2_out, or_9_out,
       S1_2_out, S1_out, S2_2_out, S2_3_out, S2_4_out, S2_5_out, S2_out, Sum_2_out, Sum_3_out, Sum_4_out,
       Sum_5_out, Sum_6_out, Sum_7_out, Sum_out, xor_1_out, xor_2_out, xor_3_out, xor_4_out, xor_5_out,
       xor_6_out, xor_7_out, xor_8_out, xor_9_out, xor_10_out;

  not not_1 (not_1_out, in_1);
  not not_2 (not_2_out, in_2);
  and A1_prime (A1_prime_out, A0_prime_out, in_1, in_2);
  and A0__B0 (A0__B0_out, A0, B0);
  not A0_prime (A0_prime_out, A0);
  and A1_B1 (A1_B1_out, A0__B0_out, in_1, not_2_out);
  or A0_B0 (A0_B0_out, A0, B0);
  or or_1 (out_20, A1_prime_out, A1_B1_out, A1_OR_B0_out, A1___B1_out);
  and A1_OR_B0 (A1_OR_B0_out, A0_B0_out, not_1_out, not_2_out);
  and A1_B1_2 (A1_B1_2_out, A1, B1);
  not A1_prime_2 (A1_prime_2_out, A1);
  and A1___B1 (A1___B1_out, xor_10_out, not_1_out, in_2);
  or A1_B1_3 (A1_B1_3_out, A1, B1);
  and A2_prime (A2_prime_out, A1_prime_2_out, in_1, in_2);
  or or_2 (out_23, A2_prime_out, A2_B2_out, A2_OR_B2_out, A2__B2_out);
  and A2_B2 (A2_B2_out, A1_B1_2_out, in_1, not_2_out);
  and A2_B2_2 (A2_B2_2_out, A2, B2);
  not A2_prime_2 (A2_prime_2_out, A2);
  and A2_OR_B2 (A2_OR_B2_out, A1_B1_3_out, not_1_out, not_2_out);
  or A2_B2_3 (A2_B2_3_out, A2, B2);
  and A2__B2 (A2__B2_out, S1_out, not_1_out, in_2);
  and A1_prime_3 (A1_prime_3_out, A2_prime_2_out, in_1, in_2);
  and A2_B2_4 (A2_B2_4_out, A3, in_14);
  not A2_prime_3 (A2_prime_3_out, A3);
  and A1_B1_4 (A1_B1_4_out, A2_B2_2_out, in_1, not_2_out);
  or A2_B2_5 (A2_B2_5_out, A3, in_14);
  or or_3 (out_21, A1_prime_3_out, A1_B1_4_out, A1_OR_B0_2_out, A1___B1_2_out);
  and A1_OR_B0_2 (A1_OR_B0_2_out, A2_B2_3_out, not_1_out, not_2_out);
  and A1___B1_2 (A1___B1_2_out, S2_out, not_1_out, in_2);
  and A0_prime_2 (A0_prime_2_out, A2_prime_3_out, in_1, in_2);
  and A0_B0_2 (A0_B0_2_out, A2_B2_4_out, in_1, not_2_out);
  or or_4 (out_22, A0_prime_2_out, A0_B0_2_out, and_1_out, A___B_out);
  and and_1 (and_1_out, A2_B2_5_out, not_1_out, not_2_out);
  and A___B (A___B_out, S2_2_out, not_1_out, in_2);
  and A1_prime_4 (A1_prime_4_out, A0_prime_3_out, in_1, in_2);
  and A1_B1_5 (A1_B1_5_out, A0__B0_2_out, in_1, not_2_out);
  or or_5 (out_24, A1_prime_4_out, A1_B1_5_out, A1_OR_B0_3_out, A1___B1_3_out);
  and A1_OR_B0_3 (A1_OR_B0_3_out, A0_B0_3_out, not_1_out, not_2_out);
  and A1___B1_3 (A1___B1_3_out, S1_2_out, not_1_out, in_2);
  not A0_prime_3 (A0_prime_3_out, A0_2);
  and A0__B0_2 (A0__B0_2_out, A0_2, B0_2);
  and A2_prime_4 (A2_prime_4_out, A1_prime_5_out, in_1, in_2);
  or A0_B0_3 (A0_B0_3_out, A0_2, B0_2);
  or or_6 (out_28, A2_prime_4_out, A2_B2_6_out, A2_OR_B2_2_out, A2__B2_2_out);
  and A2_B2_6 (A2_B2_6_out, A1_B1_6_out, in_1, not_2_out);
  not A1_prime_5 (A1_prime_5_out, A1_2);
  and A2_OR_B2_2 (A2_OR_B2_2_out, A1_B1_7_out, not_1_out, not_2_out);
  and A1_B1_6 (A1_B1_6_out, A1_2, B1_2);
  and A2__B2_2 (A2__B2_2_out, S2_3_out, not_1_out, in_2);
  or A1_B1_7 (A1_B1_7_out, A1_2, B1_2);
  and A1_prime_6 (A1_prime_6_out, A2_prime_5_out, in_1, in_2);
  not A2_prime_5 (A2_prime_5_out, A2_2);
  and A1_B1_8 (A1_B1_8_out, A2_B2_7_out, in_1, not_2_out);
  and A2_B2_7 (A2_B2_7_out, A2_2, B2_2);
  or or_7 (out_25, A1_prime_6_out, A1_B1_8_out, A1_OR_B0_4_out, A1___B1_4_out);
  and A1_OR_B0_4 (A1_OR_B0_4_out, A2_B2_8_out, not_1_out, not_2_out);
  or A2_B2_8 (A2_B2_8_out, A2_2, B2_2);
  not A2_prime_6 (A2_prime_6_out, A3_2);
  and A1___B1_4 (A1___B1_4_out, S2_4_out, not_1_out, in_2);
  and A0_prime_4 (A0_prime_4_out, A2_prime_6_out, in_1, in_2);
  and A2_B2_9 (A2_B2_9_out, A3_2, in_18);
  and A0_B0_4 (A0_B0_4_out, A2_B2_9_out, in_1, not_2_out);
  buf A2_B2_10 (A2_B2_10_out, in_18);  // OR_Gate
  or or_8 (out_26, A0_prime_4_out, A0_B0_4_out, and_2_out, A___B_2_out);
  and and_2 (and_2_out, A2_B2_10_out, not_1_out, not_2_out);
  and A___B_2 (A___B_2_out, S2_5_out, not_1_out, in_2);
  and and_3 (out_27, C3_5_out, not_1_out, in_2);
  xor xor_1 (xor_1_out, B0, in_19);
  xor xor_2 (xor_2_out, B1, in_19);
  xor xor_3 (xor_3_out, B2, in_19);
  xor xor_4 (xor_4_out, in_14, in_19);
  xor xor_5 (xor_5_out, B0_2, in_19);
  xor xor_6 (xor_6_out, B1_2, in_19);
  xor xor_7 (xor_7_out, B2_2, in_19);
  xor xor_8 (xor_8_out, in_18, in_19);
  xor xor_9 (xor_9_out, A0, xor_1_out);
  and and_4 (and_4_out, A0, xor_1_out);
  and and_5 (and_5_out, xor_9_out, in_19);
  xor Sum (Sum_out, xor_2_out, A1);
  and and_6 (and_6_out, xor_2_out, A1);
  xor Sum_2 (Sum_2_out, A2, xor_3_out);
  and and_7 (and_7_out, A2, xor_3_out);
  xor Sum_3 (Sum_3_out, A3, xor_4_out);
  and and_8 (and_8_out, A3, xor_4_out);
  xor Sum_4 (Sum_4_out, A0_2, xor_5_out);
  and and_9 (and_9_out, A0_2, xor_5_out);
  xor Sum_5 (Sum_5_out, A1_2, xor_6_out);
  and and_10 (and_10_out, A1_2, xor_6_out);
  xor Sum_6 (Sum_6_out, A2_2, xor_7_out);
  and and_11 (and_11_out, A2_2, xor_7_out);
  xor Sum_7 (Sum_7_out, A3_2, xor_8_out);
  and and_12 (and_12_out, A3_2, xor_8_out);
  and and_13 (and_13_out, or_9_out, Sum_out);
  and and_14 (and_14_out, C2_out, Sum_2_out);
  and and_15 (and_15_out, C3_out, Sum_3_out);
  and and_16 (and_16_out, C3_2_out, Sum_4_out);
  and and_17 (and_17_out, C2_2_out, Sum_5_out);
  and and_18 (and_18_out, C3_3_out, Sum_6_out);
  and and_19 (and_19_out, C3_4_out, Sum_7_out);
  xor xor_10 (xor_10_out, xor_9_out, in_19);
  or or_9 (or_9_out, and_5_out, and_4_out);
  xor S1 (S1_out, or_9_out, Sum_out);
  or C2 (C2_out, and_13_out, and_6_out);
  xor S2 (S2_out, C2_out, Sum_2_out);
  or C3 (C3_out, and_14_out, and_7_out);
  xor S2_2 (S2_2_out, C3_out, Sum_3_out);
  or C3_2 (C3_2_out, and_15_out, and_8_out);
  xor S1_2 (S1_2_out, C3_2_out, Sum_4_out);
  or C2_2 (C2_2_out, and_16_out, and_9_out);
  xor S2_3 (S2_3_out, C2_2_out, Sum_5_out);
  or C3_3 (C3_3_out, and_17_out, and_10_out);
  xor S2_4 (S2_4_out, C3_3_out, Sum_6_out);
  or C3_4 (C3_4_out, and_18_out, and_11_out);
  xor S2_5 (S2_5_out, C3_4_out, Sum_7_out);
  or C3_5 (C3_5_out, and_19_out, and_12_out);

  // Notes on the sheet:
  //   OS1 OS2
  //   0 0 = A or B
  //    0 1 = A + B
  //   1 0 = A and B
  //   1 1= A'
  //   OS1
  //   OS2
  //   4X1 Multiplexr for position 1
  //   Flip bits
  //   Output 3
  //   4X1 Multiplexr for position 1
  //   Creates complement of B if C0 =1
  //   Adds 1 to make 2s complement
  //   Creates complement of B if C0 =1
  //   Adds 1 to make 2s complement
  //   Output 2
  //   4X1 Multiplexr for position 1
  //   Output 1
  //   Output 0
  //   A OR B
  //   Collum 0 
  //   4 x 1 Multiplexer for position 0
  //   Output 3
  //   4X1 Multiplexr for position 1
  //   Output 2
  //   4X1 Multiplexr for position 1
  //   Output 1
  //   Output 0
  //   A OR B
  //   Collum 0 
  //   4 x 1 Multiplexer for position 0
  //   Carry Out
  //   C0
  //   A input
  //   1+1 = 0
  //   Creates carry if 1 + 1
  //   2nd Collumn/2nd Half adder >
  //   1 + 1 = 0
  //   Carry if A and B = 1
  //   1 + 1 = 0
  //   Carry if A and B = 1
  //   1 + 1 = 0
  //   Carry if A and B = 1
  //   2nd Collumn/2nd Half adder >
  //   1 + 1 = 0
  //   Carry if A and B = 1
  //   1 + 1 = 0
  //   Carry if A and B = 1
  //   1 + 1 = 0
  //   Carry if A and B = 1
  //   1 + 1 = 0
  //   Carry if A and B = 1
  //   if 1 + 0 + 1 = 0 + 1 carry
  //   sum + carry
  //   Carry if sum =1 carry =1
  //   Carry if sum =1 carry =1
  //   Carry if sum =1 carry =1
  //   sum + carry
  //   Carry if sum =1 carry =1
  //   Carry if sum =1 carry =1
  //   Carry if sum =1 carry =1
  //   Carry if sum =1 carry =1
  //   S0 [Sum]
  //   C1 [Carry]
  //   sum + carry
  //   sum + carry
  //   sum + carry
  //   sum + carry
  //   sum + carry
endmodule

module _8Bit_ALU___Registers (
  input  [7:0] in_1,
  input  in_2,
  input  str,
  input  ld,
  input  in_5,
  input  in_6,
  input  in_7,
  input  in_8,
  input  in_9,
  input  in_10,
  input  in_11,
  input  S0,
  input  S1,
  input  in_14,
  output Carry
);

  wire clock_1_out, clock_2_out, clock_3_out, clock_4_out, clock_5_out, clock_6_out, clock_7_out,
       clock_8_out, clock_9_out, clock_10_out;
  wire [7:0] controlled_buffer_1_out, n8_bit_alu_1_out_20, ram_1_data, register_2_q, register_3_q,
       register_4_q, register_5_q, register_6_q, register_7_q, register_8_q, register_9_q;

  assign controlled_buffer_1_out = in_2 ? in_1 : 8'bz;  // Controlled_Buffer controlled_buffer_1
  Register register_1 (.D(controlled_buffer_1_out), .clk(clock_1_out));  // open: en, Q, clr
  Clock clock_1 (.out(clock_1_out));
  Clock clock_2 (.out(clock_2_out));
  DotMatrix #(.inputtype("row"), .matrixcols(8), .matrixrows(1)) dotmatrix_1 (.row0(register_2_q));
  Register register_2 (.D(controlled_buffer_1_out), .Q(register_2_q), .clk(clock_2_out));  // open: en, clr
  assign controlled_buffer_1_out = in_6 ? register_2_q : 8'bz;  // Controlled_Buffer controlled_buffer_2
  Register register_3 (.D(controlled_buffer_1_out), .Q(register_3_q), .clk(clock_3_out));  // open: en, clr
  Clock clock_3 (.out(clock_3_out));
  DotMatrix #(.inputtype("row"), .matrixcols(8), .matrixrows(1)) dotmatrix_2 (.row0(register_3_q));
  assign controlled_buffer_1_out = in_7 ? register_3_q : 8'bz;  // Controlled_Buffer controlled_buffer_3
  Register register_4 (.D(controlled_buffer_1_out), .Q(register_4_q), .clk(clock_4_out));  // open: en, clr
  Clock clock_4 (.out(clock_4_out));
  DotMatrix #(.inputtype("row"), .matrixcols(8), .matrixrows(1)) dotmatrix_3 (.row0(register_4_q));
  DotMatrix #(.inputtype("row"), .matrixcols(8), .matrixrows(1)) dotmatrix_4 (.row0(register_5_q));
  assign controlled_buffer_1_out = in_8 ? register_4_q : 8'bz;  // Controlled_Buffer controlled_buffer_4
  Register register_5 (.D(controlled_buffer_1_out), .Q(register_5_q), .clk(clock_5_out));  // open: en, clr
  Clock clock_5 (.out(clock_5_out));
  assign controlled_buffer_1_out = in_9 ? register_5_q : 8'bz;  // Controlled_Buffer controlled_buffer_5
  DotMatrix #(.inputtype("row"), .matrixcols(8), .matrixrows(1)) dotmatrix_5 (.row0(register_6_q));
  Register register_6 (.D(controlled_buffer_1_out), .Q(register_6_q), .clk(clock_6_out));  // open: en, clr
  Clock clock_6 (.out(clock_6_out));
  assign controlled_buffer_1_out = in_10 ? register_6_q : 8'bz;  // Controlled_Buffer controlled_buffer_6
  DotMatrix #(.inputtype("row"), .matrixcols(8), .matrixrows(1)) dotmatrix_6 (.row0(register_7_q));
  Register register_7 (.D(controlled_buffer_1_out), .Q(register_7_q), .clk(clock_7_out));  // open: en, clr
  Clock clock_7 (.out(clock_7_out));
  DotMatrix #(.inputtype("row"), .matrixcols(8), .matrixrows(1)) dotmatrix_7 (.row0(register_8_q));
  Register register_8 (.D(controlled_buffer_1_out), .Q(register_8_q), .clk(clock_8_out));  // open: en, clr
  Clock clock_8 (.out(clock_8_out));
  DotMatrix #(.inputtype("row"), .matrixcols(8), .matrixrows(1)) dotmatrix_8 (.row0(n8_bit_alu_1_out_20));
  _8_bit_ALU u_8_bit_alu_1 (
    .A0(register_8_q[0]), .A1(register_8_q[1]), .A2(register_8_q[2]), .A3(register_8_q[3]),
    .A0_2(register_8_q[4]), .A1_2(register_8_q[5]), .A2_2(register_8_q[6]), .A3_2(register_8_q[7]),
    .B0(register_7_q[0]), .B1(register_7_q[1]), .B2(register_7_q[2]), .in_14(register_7_q[3]),
    .B0_2(register_7_q[4]), .B1_2(register_7_q[5]), .B2_2(register_7_q[6]), .in_18(register_7_q[7]),
    .out_20(n8_bit_alu_1_out_20[0]), .out_23(n8_bit_alu_1_out_20[1]), .out_21(n8_bit_alu_1_out_20[2]),
    .out_22(n8_bit_alu_1_out_20[3]), .out_24(n8_bit_alu_1_out_20[4]), .out_28(n8_bit_alu_1_out_20[5]),
    .out_25(n8_bit_alu_1_out_20[6]), .out_26(n8_bit_alu_1_out_20[7]), .in_1(S0), .in_2(S1), .in_19(in_14),
    .out_27(Carry));
  assign controlled_buffer_1_out = in_5 ? n8_bit_alu_1_out_20 : 8'bz;  // Controlled_Buffer controlled_buffer_7
  Register register_9 (.D(controlled_buffer_1_out), .Q(register_9_q), .clk(clock_9_out));  // open: en, clr
  Clock clock_9 (.out(clock_9_out));
  Clock clock_10 (.out(clock_10_out));
  RAM #(.bus("separate")) ram_1 (
    .addr(register_9_q), .din(controlled_buffer_1_out), .data(ram_1_data), .str(str), .clk(clock_10_out),
    .ld(ld));  // open: sel, clr
  assign controlled_buffer_1_out = in_11 ? ram_1_data : 8'bz;  // Controlled_Buffer controlled_buffer_8

  // Notes on the sheet:
  //   IR
  //   Made by Ricky Flores
  //   PC
  //   Registers
  //   B
  //   A
  //   A + B =
  //   S0
  //   8 Bit ALU
  //   S1
  //   0 0 = A or B
  //    0 1 = A + B
  //   1 0 = A and B
  //   1 1= A'
  //   B' + 1 (2s complemnt)
  //   data in
  //   address
  //   data out
endmodule
